# Fritzing sketch Schematy (saved by Fritzing 1.0.6)
breadboards: 1

parts:
  Arduino_Uno = Arduino Uno (Rev3) - ICSP
  Akcelerometr = Grove 3 Axis Digital Accelerometer 16g
  Przycisk = Grove Button
  Buzzer = Grove Buzz
  Potencjometr = Grove Rotary Angle Sensor
  LED1 = smd LED [color="Red (633nm)" package="0603 [SMD]"]
  R1 = Resistor [tolerance=±5% power=0.25W resistance=220 package=THT]
  OLED = Grove OLED 128x96

nets:
  N1: Arduino_Uno.A0, Potencjometr.SIG
  N2: Arduino_Uno.A4/SDA, Akcelerometr.SDA, OLED.SDA
  N3: Arduino_Uno.A5/SCL, Akcelerometr.SCL, OLED.SCL
  GND: Arduino_Uno.GND, Akcelerometr.GND, Przycisk.GND, Buzzer.GND, Potencjometr.GND, LED1.cathode, OLED.GND
  N4: Arduino_Uno.D4, R1.Pin_0
  N5: Arduino_Uno.D5_PWM, Buzzer.SIG
  N6: Arduino_Uno.D6_PWM, Przycisk.SIG
  5V: Arduino_Uno.5V, Akcelerometr.VCC, Przycisk.VCC, Buzzer.VCC, Potencjometr.VCC, OLED.VCC
  N7: LED1.anode, R1.Pin_1

custom parts:
  Grove Rotary Angle Sensor: A potentiometer
